# Fritzing sketch RPi Arduino Wire Up (Fritzing) (saved by Fritzing 0.9.3b)

parts:
  Bauteil1 = Arduino Uno (Rev3)
  C1 = Ceramic Capacitor [capacitance=1µF package="100 mil [THT, multilayer]"]
  Raspberry_Pi1 = Raspberry Pi 2
  R1 = Resistor [tolerance=±5% resistance=10k package=THT]
  R2 = Resistor [tolerance=±5% resistance=15k package=THT]

nets:
  N1: Bauteil1.D0/RX, Raspberry_Pi1.GPIO14
  N2: Bauteil1.D1/TX, R1.Pin_0
  N3: Bauteil1.RESET, C1.1
  GND: Bauteil1.GND, Raspberry_Pi1.GND, R2.Pin_1
  N4: C1.0, Raspberry_Pi1.GPIO4
  N5: Raspberry_Pi1.GPIO15, R1.Pin_1, R2.Pin_0

notes:
  Arduino TX
  Voltage divider (5V -> 3.3V)
  Raspberry RX
  Raspberry TX
  Arduino RX
  Raspberry GPIO 4
  1uF Capacitor
  Arduino RESET
  If programming directly to an ATmega328 a 100nF capacitor is sufficient.
  Common GND
